# Fritzing sketch dds_schematic (saved by Fritzing 0.9.4)

parts:
  Arduino_Nano = Arduino Nano (Rev3.0)
  Pantalla_LCD = LCD-16X2 [package=lcd-16x2_noholes]
  R1 = Trimmer Potentiometer [maximum_resistance=10kΩ part_number=Contraste package=THT]
  Encoder_VFO = Rotary Encoder with switch (KY-040) [part_number=KY-040]
  DDS = DDS AD9850
  Selector_bandas = Rotary_Switch_3P3T [package="Panel Mount"]
  IC1 = Voltage Regulator [part_number=7805 package=78xxl]
  C1 = Electrolytic Capacitor [capacitance=100µF voltage=10V package="100 mil [THT, electrolytic]"]
  R2 = Resistor [tolerance=±5% resistance=100k package=THT]
  R3 = Resistor [tolerance=±5% resistance=680k package=THT]
  C2 = Ceramic Capacitor [capacitance=33nF package="100 mil [THT, multilayer]"]
  C3 = Ceramic Capacitor [capacitance=10nF package="100 mil [THT, multilayer]"]
  D1 = Rectifier Diode [part_number=1N4148 package="300 mil [THT]"]
  R4 = Resistor [tolerance=±5% resistance=1.5M package=THT]
  C4 = Ceramic Capacitor [capacitance=10nF package="100 mil [THT, multilayer]"]
  C5 = Ceramic Capacitor [capacitance=100nF package="100 mil [THT, multilayer]"]

nets:
  GND: Arduino_Nano.GND, Pantalla_LCD.VSS, Pantalla_LCD.R_W, Pantalla_LCD.K, R1.leg1, Encoder_VFO.GND, DDS.GND, Selector_bandas.9, IC1.GND, C1.-, R3.Pin_0, C2.0, C3.0, C4.0
  N1: Arduino_Nano.D2, Encoder_VFO.CLK
  N2: Arduino_Nano.D3, Encoder_VFO.DT
  N3: Arduino_Nano.D4, Pantalla_LCD.DB7
  N4: Arduino_Nano.D5, Pantalla_LCD.DB6
  N5: Arduino_Nano.D6, Pantalla_LCD.DB5
  N6: Arduino_Nano.D7, Pantalla_LCD.DB4
  N7: Arduino_Nano.D8, DDS.CLK
  N8: Arduino_Nano.D9, DDS.FQ
  N9: Arduino_Nano.D10, DDS.DATA
  N10: Arduino_Nano.D11/MOSI, DDS.RST
  N11: Arduino_Nano.D12/MISO, Pantalla_LCD.RS
  N12: Arduino_Nano.5V, IC1.OUT, C1.+
  N13: Arduino_Nano.A5, R2.Pin_1, R3.Pin_1, C2.1
  N14: Arduino_Nano.A4, R4.Pin_1, C4.1
  N15: Arduino_Nano.A3, Encoder_VFO.SW
  N16: Arduino_Nano.A2, Selector_bandas.12
  N17: Arduino_Nano.A1, Selector_bandas.11
  N18: Arduino_Nano.A0, Selector_bandas.10
  N19: Arduino_Nano.D13/SCK, Pantalla_LCD.E
  VDD: Pantalla_LCD.VDD, Pantalla_LCD.A, DDS.VCC
  N20: Pantalla_LCD.VO, R1.wiper
  N21: DDS.SINB, C5.0
  Desde el DDS: Selector_bandas.5
  12V: IC1.IN
  N22: R2.Pin_0, C3.1, D1.cathode
  Led rojo TX: D1.anode
  Pin 7 (AGC): R4.Pin_0
  Al selector de bandas: C5.1

custom parts:
  Rotary Encoder with switch (KY-040): A Rotary Encoder with switch
  DDS AD9850: AD9850 DDS Signal Generator Module, frequency range 0 to 40MHz, sine or square wave output, on board 70MHz low pass filter, and 125MHz clock module. https://code.google.com/p/ad9850-arduino/
  Rotary_Switch_3P3T: Rotary Switch with 3 Poles, each with 3 Positions
